# Fritzing sketch AnalogInputFSR (saved by Fritzing 0.1.b)
breadboards: 1

parts:
  Arduino1 = Arduino Diecimila (deprecated) [package=THT]
  LED1 = Red LED - 5mm
  J1 = Basic Force Sensing Resistor (FSR) [package=THT]
  R1 = basic-resistor-10k

nets:
  N1: Arduino1.GND, LED1.cathode, R1.connector0
  N2: Arduino1.D13, LED1.anode
  N3: Arduino1.+5V, J1.pin_0
  N4: Arduino1.A2, J1.pin_1, R1.connector1
