# Fritzing sketch AnalogInputOutput (saved by Fritzing 0.1.14)
breadboards: 1

parts:
  Arduino1 = Arduino Diecimila (deprecated) [package=THT]
  LED1 = Red LED - 5mm
  R2 = 220 Ω Resistor [package=THT]
  R3 = Rotary Potentiometer (Large) [package=THT]

nets:
  N1: Arduino1.GND, LED1.cathode, R3.leg2
  N2: Arduino1.D3, R2.Pin_1
  N3: Arduino1.+5V, R3.leg1
  N4: Arduino1.A3, R3.wiper
  N5: LED1.anode, R2.Pin_0
