# Fritzing sketch AnalogInputToServo (saved by Fritzing 0.1.b)
breadboards: 1

parts:
  Arduino1 = Arduino Diecimila (deprecated) [package=THT]
  J1 = Basic Servo
  R1 = Trimmer Potentiometer [package=THT]

nets:
  N1: Arduino1.D2, J1.pulse
  +5V: Arduino1.+5V, J1.vcc, R1.leg1
  GND: Arduino1.GND, Arduino1.ground, J1.gnd, R1.leg2
  N2: Arduino1.A2, R1.wiper
