# Fritzing sketch Blink (saved by Fritzing 0.1.b)

parts:
  Part1 = Arduino Diecimila (deprecated) [package=THT]
  LED1 = Red LED - 5mm

nets:
  N1: Part1.GND, Part1.ground, LED1.cathode
  N2: Part1.D13, LED1.anode
