# Fritzing sketch Loop (saved by Fritzing 0.1.b)
breadboards: 1

parts:
  Arduino1 = Arduino Diecimila (deprecated) [package=THT]
  R1 = basic-resistor-220
  LED1 = Red LED - 5mm
  LED2 = Red LED - 5mm
  R2 = basic-resistor-220
  LED3 = Red LED - 5mm
  R3 = basic-resistor-220
  LED4 = Red LED - 5mm
  R4 = basic-resistor-220
  LED5 = Red LED - 5mm
  R5 = basic-resistor-220
  LED6 = Red LED - 5mm
  R6 = basic-resistor-220

nets:
  N1: Arduino1.GND, LED1.cathode, LED2.cathode, LED3.cathode, LED4.cathode, LED5.cathode, LED6.cathode
  N2: Arduino1.D7, R1.connector1
  N3: Arduino1.D6, R2.connector1
  N4: Arduino1.D5, R3.connector1
  N5: Arduino1.D4, R4.connector1
  N6: Arduino1.D3, R5.connector1
  N7: Arduino1.D2, R6.connector1
  N8: R1.connector0, LED1.anode
  N9: LED2.anode, R2.connector0
  N10: LED3.anode, R3.connector0
  N11: LED4.anode, R4.connector0
  N12: LED5.anode, R5.connector0
  N13: LED6.anode, R6.connector0
