# Fritzing sketch npnPowerTransistor (saved by Fritzing 0.1.b)
breadboards: 1

parts:
  Arduino1 = Arduino Diecimila (deprecated) [package=THT]
  Q1 = npn-Powertransistor [package="TO220 [THT]"]
  R1 = basic-resistor-1k
  LED1 = Red LED - 5mm
  R2 = basic-resistor-220
  LED2 = Red LED - 5mm
  R3 = basic-resistor-220
  LED4 = Red LED - 5mm
  R4 = basic-resistor-220
  R4_2 = basic-resistor-220  # not connected
  R4_3 = basic-resistor-220
  LED5 = Red LED - 5mm
  R5 = basic-resistor-220

nets:
  N1: Arduino1.GND, Q1.emitter
  N2: Arduino1.D12, R1.connector0
  N3: Arduino1.+5V, R2.connector1, R3.connector1, R4.connector1, R4_3.connector1, R5.connector1
  N4: Q1.base, R1.connector1
  N5: Q1.collector, LED1.cathode, LED2.cathode, LED4.cathode, LED5.cathode
  N6: LED1.anode, R2.connector0
  N7: LED2.anode, R3.connector0
  N8: LED4.anode, R4.connector0, R4_3.connector0
  N9: LED5.anode, R5.connector0
