# Fritzing sketch Photocell (saved by Fritzing 0.3.0)
breadboards: 1

parts:
  R1 = Basic Photo-Resistor (Photocell) [package=THT]
  R2 = 1k Ω Resistor [package=THT]
  R3 = 220 Ω Resistor [package=THT]
  LED1 = Red LED - 5mm
  R4 = 220 Ω Resistor [package=THT]
  Arduino1 = Arduino

nets:
  N1: R1.pin_0, Arduino1.+5V
  N2: R1.pin_1, R2.Pin_0, R3.Pin_1
  N3: R2.Pin_1, Arduino1.A2
  N4: R3.Pin_0, LED1.cathode, Arduino1.GND
  N5: LED1.anode, R4.Pin_1
  N6: R4.Pin_0, Arduino1.D2
