# Fritzing sketch TouchSwitch (saved by Fritzing 0.3.4b)
breadboards: 1

parts:
  Q1 = NPN-Transistor [package="TO92 [THT]"]
  Q1_2 = NPN-Transistor [package="TO92 [THT]"]
  R3 = 10k Ω Resistor [package=THT]
  R4 = 1k Ω Resistor [package=THT]
  R3_2 = 10k Ω Resistor [package=THT]
  Arduino1 = Arduino
  LED1 = Red LED - 5mm

nets:
  N1: Q1.emitter, R4.Pin_0
  N2: Q1.collector, R3.Pin_0
  N3: Q1_2.emitter, R3_2.Pin_0, Arduino1.A0
  N4: Q1_2.base, R3.Pin_1
  N5: Q1_2.collector, Arduino1.GND, LED1.cathode
  N6: R4.Pin_1, R3_2.Pin_1, Arduino1.+5V
  N7: Arduino1.D13, LED1.anode

notes:
  A simple touch switch can be created by using two NPN transistors. When touching the two blue cables, the LED will turn on. (download code from the project page)
  http://en.wikipedia.org/wiki/Darlington_transistor
