# Fritzing sketch VoltageRegulator_7800series (saved by Fritzing 0.3.0)
breadboards: 1

parts:
  C1 = Electrolytic Capacitor [package=THT]
  C2 = Electrolytic Capacitor [package=THT]
  U1 = Voltage Regulator - 5V [package="TO220 [THT]"]
  VCC1 = obsolete Battery

nets:
  N1: C1.-, C2.-, U1.GND, VCC1.-
  N2: C1.+, U1.input_voltage, VCC1.+
  N3: C2.+, U1.output_voltage

notes:
  This example uses a 7805 voltage regulator to regulate voltage to 5volts. The battery should be at least 7v (we don't have the part yet).
