# Fritzing sketch Window_Alarm (saved by Fritzing 0.2.2)
breadboards: 1

parts:
  Arduino1 = Arduino Diecimila (deprecated) [package=THT]
  S1 = Reed switch [package=THT]
  R1 = 10k Ω Resistor [package=THT]
  J1 = Piezo Speaker

nets:
  N1: Arduino1.GND, R1.Pin_1, J1.pin1
  N2: Arduino1.D12, S1.pin_1, R1.Pin_0
  N3: Arduino1.D9, J1.pin2
  N4: Arduino1.+5V, S1.pin_2

notes:
  Reed switches close when a magnet is placed near their casing. In this example, a magnet could be mounted on a window and the reed switch on the windowsill so that everytime the window was opened, the piezo buzzer would sound.
